# Fritzing sketch sn74hc595-led-bar-graph-double-up (saved by Fritzing 0.9.4)
breadboards: 1

parts:
  Raspberry_Pi_1 = Raspberry Pi 3 [part_number=RPI-3-V1.2]
  U1 = 74HC595 [package="DIP16 [THT]"]
  D1 = LED_BARGRAPH_10 [package=led_bargaph_10]
  R1 = Resistor [tolerance=±5% resistance=220 package="1206 [SMD]"]
  R2 = Resistor [tolerance=±5% resistance=220 package="1206 [SMD]"]
  R3 = Resistor [tolerance=±5% resistance=220 package="1206 [SMD]"]
  R4 = Resistor [tolerance=±5% resistance=220 package="1206 [SMD]"]
  R7 = Resistor [tolerance=±5% resistance=220 package="1206 [SMD]"]
  R9 = Resistor [tolerance=±5% resistance=220 package="1206 [SMD]"]
  U2 = 74HC595 [package="DIP16 [THT]"]
  D2 = LED_BARGRAPH_10 [package=led_bargaph_10]
  R11 = Resistor [tolerance=±5% resistance=220 package="1206 [SMD]"]
  R12 = Resistor [tolerance=±5% resistance=220 package="1206 [SMD]"]
  R13 = Resistor [tolerance=±5% resistance=220 package="1206 [SMD]"]
  R14 = Resistor [tolerance=±5% resistance=220 package="1206 [SMD]"]
  R15 = Resistor [tolerance=±5% resistance=220 package="1206 [SMD]"]
  R16 = Resistor [tolerance=±5% resistance=220 package="1206 [SMD]"]
  R18 = Resistor [tolerance=±5% resistance=220 package="1206 [SMD]"]
  R19 = Resistor [tolerance=±5% resistance=220 package="1206 [SMD]"]
  R20 = Resistor [tolerance=±5% resistance=220 package="1206 [SMD]"]
  R21 = Resistor [tolerance=±5% resistance=220 package="1206 [SMD]"]
  R22 = Resistor [tolerance=±5% resistance=220 package="1206 [SMD]"]

nets:
  N1: Raspberry_Pi_1.GPIO10, U1.MR, U2.MR
  N2: Raspberry_Pi_1.GPIO11, U1.SH_CP, U2.SH_CP
  N3: Raspberry_Pi_1.GPIO13, U1.OE, U2.OE
  N4: Raspberry_Pi_1.GPIO12, U1.ST_CP, U2.ST_CP
  GND: Raspberry_Pi_1.GND, Raspberry_Pi_1.GPIO14, U1.GND, U1.DS, R1.Pin_0, R2.Pin_0, R3.Pin_0, R4.Pin_0, R7.Pin_0, R9.Pin_0, U2.GND, R11.Pin_0, R12.Pin_0, R13.Pin_0, R14.Pin_0, R15.Pin_0, R16.Pin_0, R18.Pin_0, R19.Pin_0, R20.Pin_0, R21.Pin_0, R22.Pin_0
  VCC: Raspberry_Pi_1.5V, U1.VCC, U2.VCC
  N5: U1.Q1, D1.B_A
  N6: U1.Q2, D1.C_A
  N7: U1.Q3, D1.D_A
  N8: U1.Q4, D1.E_A
  N9: U1.Q5, D1.F_A
  N10: U1.Q6, D1.G_A
  N11: U1.Q7, D1.H_A
  N12: U1.Q7', U2.DS
  N13: U1.Q0, D1.A_A
  N14: D1.I_A, U2.Q0
  N15: D1.J_A, U2.Q1
  N16: D1.J_C, R12.Pin_1
  N17: D1.I_C, R11.Pin_1
  N18: D1.H_C, R7.Pin_1
  N19: D1.G_C, R1.Pin_1
  N20: D1.F_C, D2.G_C, R20.Pin_1
  N21: D1.E_C, R16.Pin_1
  N22: D1.D_C, R9.Pin_1
  N23: D1.C_C, R4.Pin_1
  N24: D1.B_C, R2.Pin_1
  N25: D1.A_C, R3.Pin_1
  N26: U2.Q2, D2.A_A
  N27: U2.Q3, D2.B_A
  N28: U2.Q4, D2.C_A
  N29: U2.Q5, D2.D_A
  N30: U2.Q6, D2.E_A
  N31: U2.Q7, D2.F_A
  N32: D2.J_C, D2.B_C, R22.Pin_1
  N33: D2.I_C, D2.H_C, R21.Pin_1
  N34: D2.F_C, R19.Pin_1
  N35: D2.E_C, R18.Pin_1
  N36: D2.D_C, R14.Pin_1
  N37: D2.C_C, R13.Pin_1
  N38: D2.A_C, R15.Pin_1
