# Fritzing sketch test_setup (saved by Fritzing 1.0.1rc)
breadboards: 1

parts:
  Mod1 = Raspberry Pi 4B
  R1 = Resistor [tolerance=±5% resistance=10k package="0402 [SMD]"]
  R2 = Resistor [tolerance=±5% power=0.25W resistance=47 package=THT]
  LED = LED - 3mm [color="Red (633nm)" current=0.030A package="3 mm [THT]"]
  C1 = Electrolytic Capacitor [capacitance=1000µF voltage=35V package="300 mil [THT, electrolytic]"]
  Q2 = NPN-Transistor [package="TO92 [THT]"]
  Adafruit_VCNL1 = Adafruit VCNL4040

nets:
  3V3: Mod1.3V3, R1.Pin_1, R2.Pin_1, C1.+, Adafruit_VCNL1.3.3V
  N1: Mod1.GPIO2, Adafruit_VCNL1.SDA
  N2: Mod1.GPIO3, Adafruit_VCNL1.SCL
  GND: Mod1.GND, C1.-, Q2.E, Adafruit_VCNL1.GND
  N3: R1.Pin_0, Q2.B, Adafruit_VCNL1.INT
  N4: R2.Pin_0, LED.anode
  N5: LED.cathode, Q2.C
